# Fritzing sketch mechane (saved by Fritzing 0.8.3b)
breadboards: 3

parts:
  motor = DC Motor
  CPU = atmega168 [package=dip]
  motor_driver = H-Bridge [package=THT]
  battery = LIPO-2000mAh [package=lipo-2000]
  3_3v_reg = V_REG_LD1117VXX [package=78xxl]
  isp_header = AVR_MINI_PROG [package=avr_mini_prog]
  radio = RFM12b HopeRF Transceiver
  defaults = Solder Jumper [package=sj_2s]
  status_(connection) = smd LED [color="Red (633nm)" package="0603 [SMD]"]
  reset = Solder Jumper [package=sj_2s]
  baud=9600 = Solder Jumper [package=sj_2s]
  status_(rx/tx) = smd LED [color="Red (633nm)" package="0603 [SMD]"]
  Bluetooth = RN-42 SMD [chip_label=IC package=QFN-32]

nets:
  N1: motor.pin_1, motor_driver.2Y, motor_driver.3Y
  N2: motor.pin_2, motor_driver.1Y, motor_driver.4Y
  reset: CPU.RESET, isp_header.RST
  N3: CPU.D0_(RX), Bluetooth.UART_TX
  N4: CPU.D1_(TX), Bluetooth.UART_RX
  N5: CPU.D2, radio.2_nIRQ
  N6: CPU.D3_(PWM), radio.14_nSEL
  3.3v: CPU.VCC, CPU.AVCC, motor_driver.VCC1, 3_3v_reg.OUT, radio.3_FSK/DATA, radio.9_VDD, defaults.2, baud=9600.2, Bluetooth.VDD
  GND: CPU.GND, motor_driver.GND1, motor_driver.GND2, motor_driver.GND3, motor_driver.GND4, battery.-, 3_3v_reg.GND, isp_header.GND, radio.7_GND, radio.10_GND, status_(connection).anode, reset.2, status_(rx/tx).cathode, Bluetooth.GND
  mosi: CPU.D11_(PWM), isp_header.MOSI, radio.12_SDI
  miso: CPU.D12, isp_header.MISO, radio.1_SDO
  sck: CPU.D13, isp_header.SCK, radio.13_SCK
  N7: CPU.A0, motor_driver.1A, motor_driver.4A
  N8: CPU.A1, motor_driver.2A, motor_driver.3A
  N9: CPU.A2, motor_driver.1_2EN, motor_driver.3_4EN
  batt: motor_driver.VCC2, battery.+, 3_3v_reg.IN
  N10: defaults.1, Bluetooth.PIO4
  N11: status_(connection).cathode, Bluetooth.PIO2
  N12: reset.1, Bluetooth.RESET
  N13: baud=9600.1, Bluetooth.PIO7
  N14: status_(rx/tx).anode, Bluetooth.PIO8

custom parts:
  RFM12b HopeRF Transceiver: RF Transceiver by Hope RF. Well supported Arduino libraries are available. Part is available in several frequencies (433MHz, 915MHz)...
  RN-42 SMD: This is the surface mount RN-42 part
